// Logisim project f8ful.circ as structural Verilog: 10 circuits, main circuit register_bank
module main (
);

  wire alu_1_rc, alu_1_re, alu_1_rg, alu_1_rl, alu_1_rz, alu_1_sc, alu_1_se, alu_1_sg, alu_1_sl, alu_1_sz,
       and_2_out, and_3_out, button_1_out, C, CLK_out, control_1_ahi, control_1_ali, control_1_ao,
       control_1_aoh, control_1_aol, control_1_aom, control_1_la, control_1_lsp, control_1_rbi,
       control_1_rbo, control_1_sa, control_1_spd, control_1_spi, control_1_sr, control_1_thl,
       memory_bank_1_pr, memory_bank_1_pw, por_1_out, R, RESET_out;
  wire [2:0] control_1_rs, control_1_rsp;
  wire [4:0] memory_bank_1_ps;
  wire [7:0] B, controlled_buffer_1_out, controlled_buffer_2_out, memory_bank_1_ho, memory_bank_1_lo,
       memory_bank_1_po, ports_1_pao, ports_1_po, register_bank_1_ho, register_bank_1_lo, sreg_1_z;
  wire [7:1] undriven;

  POR #(.PorHighDuration(1), .porsize(2)) por_1 (.out(por_1_out));
  or or_1 (R, por_1_out, RESET_out);
  Button RESET (.out(RESET_out));
  Clock CLK (.out(CLK_out));
  and and_1 (C, ~R, CLK_out);  // AND_Gate
  alu alu_1 (
    .AO(control_1_ao), .AOH(control_1_aoh), .AOM(control_1_aom), .AOL(control_1_aol), .BI(B), .CLK(C),
    .RESET(R), .CI(sreg_1_z[1]), .SZ(alu_1_sz), .RZ(alu_1_rz), .SC(alu_1_sc), .RC(alu_1_rc), .BO(B),
    .SL(alu_1_sl), .RL(alu_1_rl), .SE(alu_1_se), .RE(alu_1_re), .SG(alu_1_sg), .RG(alu_1_rg));
  control control_1 (
    .AL(memory_bank_1_lo), .AH(memory_bank_1_ho), .LI(register_bank_1_lo), .HI(register_bank_1_ho),
    .Z(sreg_1_z[0]), .RESET(R), .CLK(C), .SPI(control_1_spi), .SPD(control_1_spd), .SR(control_1_sr), .BO(B),
    .LSP(control_1_lsp), .AHI(control_1_ahi), .ALI(control_1_ali), .SA(control_1_sa), .LA(control_1_la),
    .THL(control_1_thl), .AOL(control_1_aol), .AOM(control_1_aom), .AOH(control_1_aoh), .AO(control_1_ao),
    .RBI(control_1_rbi), .RBO(control_1_rbo), .RS(control_1_rs), .RSP(control_1_rsp));
  sreg sreg_1 (
    .SZ(alu_1_sz), .RZ(alu_1_rz), .SG(alu_1_sg), .RG(alu_1_rg), .SE(alu_1_se), .RE(alu_1_re), .SL(alu_1_sl),
    .RL(alu_1_rl), .SC(alu_1_sc), .RC(alu_1_rc), .RESET(R), .Z(sreg_1_z[0]), .G(sreg_1_z[4]),
    .E(sreg_1_z[3]), .L(sreg_1_z[2]), .C(sreg_1_z[1]), .H(sreg_1_z[7]));  // open: SH, RH
  memory_bank memory_bank_1 (
    .SREG(sreg_1_z), .PI(ports_1_po), .DI(B), .ALI(control_1_ali), .AHI(control_1_ahi), .LA(control_1_la),
    .SA(control_1_sa), .CLK(C), .THL(control_1_thl), .RBO(control_1_rbo), .HI(controlled_buffer_1_out),
    .LI(controlled_buffer_2_out), .RESET(R), .SPD(control_1_spd), .SPI(control_1_spi), .LSP(control_1_lsp),
    .PO(memory_bank_1_po), .PS(memory_bank_1_ps), .DO(B), .PR(memory_bank_1_pr), .PW(memory_bank_1_pw),
    .HO(memory_bank_1_ho), .LO(memory_bank_1_lo));
  register_bank register_bank_1 (
    .HI(controlled_buffer_1_out), .LI(controlled_buffer_2_out), .RESET(R), .DI(B), .RBO(control_1_rbo),
    .RBI(control_1_rbi), .RS(control_1_rs), .CLK(C), .THL(control_1_thl), .RSB(control_1_rsp),
    .SR(control_1_sr), .DO(B), .HO(register_bank_1_ho), .LO(register_bank_1_lo));
  assign controlled_buffer_1_out = and_2_out ? memory_bank_1_ho : 8'bz;  // Controlled_Buffer controlled_buffer_1
  assign controlled_buffer_2_out = and_2_out ? memory_bank_1_lo : 8'bz;  // Controlled_Buffer controlled_buffer_2
  and and_2 (and_2_out, control_1_rbi, control_1_thl);
  assign controlled_buffer_1_out = and_3_out ? register_bank_1_ho : 8'bz;  // Controlled_Buffer controlled_buffer_3
  assign controlled_buffer_2_out = and_3_out ? register_bank_1_lo : 8'bz;  // Controlled_Buffer controlled_buffer_4
  and and_3 (and_3_out, control_1_rbo, control_1_thl);
  ports ports_1 (
    .PS(memory_bank_1_ps), .WRITE(memory_bank_1_pw), .READ(memory_bank_1_pr), .PAI({undriven, 1'b0}),
    .CLK(C), .DI(memory_bank_1_po), .RESET(R), .PAO(ports_1_pao), .PO(ports_1_po));
  // LedBar #(.inputtype("row")) ledbar_1: pin names not known; wires that end beside it: ports_1_pao
  Button button_1 (.out(button_1_out));
  Transistor #(.\type ("n")) transistor_1 (.in(1'b0), .gate(button_1_out));  // open: out
endmodule

// RB
module register_bank (
  input  [7:0] HI,
  input  [7:0] LI,
  input  RESET,
  input  [7:0] DI,
  input  RBO,
  input  RBI,
  input  [2:0] RS,
  input  CLK,
  input  THL,
  input  [2:0] RSB,
  input  SR,
  output [7:0] DO,
  output [7:0] HO,
  output [7:0] LO
);

  wire and_1_out, and_2_out, and_3_out, and_4_out, and_5_out, and_6_out, and_7_out, and_8_out, and_9_out,
       and_10_out, and_11_out, and_12_out, and_13_out, and_14_out, and_15_out, and_16_out, and_17_out,
       and_18_out, demultiplexer_1_out0, demultiplexer_1_out1, demultiplexer_1_out2, demultiplexer_1_out3,
       demultiplexer_1_out4, demultiplexer_1_out5, demultiplexer_1_out6, demultiplexer_1_out7, not_1_out,
       or_1_out, or_2_out, or_3_out, or_4_out, or_5_out, or_6_out, or_7_out, or_8_out, or_9_out,
       pull_resistor_1_node, pull_resistor_2_node, pull_resistor_3_node, pull_resistor_4_node,
       pull_resistor_5_node, pull_resistor_6_node, pull_resistor_7_node, pull_resistor_8_node;
  wire [7:0] A_q, B_q, C_q, controlled_buffer_1_out, D_q, E_q, F_q;

  not not_1 (not_1_out, THL);
  and and_1 (and_1_out, RBI, ~THL);  // AND_Gate
  and and_2 (and_2_out, and_1_out, demultiplexer_1_out3);
  and and_3 (and_3_out, and_1_out, demultiplexer_1_out2);
  and and_4 (and_4_out, and_1_out, demultiplexer_1_out1);
  and and_5 (and_5_out, and_1_out, demultiplexer_1_out0);
  and and_6 (and_6_out, RBI, THL);
  Register #(.trigger("falling")) D (.D(DI), .en(or_1_out), .clk(CLK), .Q(D_q), .clr(RESET));
  or or_1 (or_1_out, and_2_out, pull_resistor_4_node);
  Register #(.trigger("falling")) C (.D(DI), .en(or_2_out), .clk(CLK), .Q(C_q), .clr(RESET));
  or or_2 (or_2_out, and_3_out, pull_resistor_3_node);
  Register #(.trigger("falling")) B (.D(DI), .en(or_3_out), .clk(CLK), .Q(B_q), .clr(RESET));
  or or_3 (or_3_out, and_4_out, pull_resistor_2_node);
  Register #(.trigger("falling")) A (.D(DI), .en(or_4_out), .clk(CLK), .Q(A_q), .clr(RESET));
  or or_4 (or_4_out, and_5_out, pull_resistor_1_node);
  or or_5 (or_5_out, RBO, SR);
  assign controlled_buffer_1_out = and_7_out ? D_q : 8'bz;  // Controlled_Buffer controlled_buffer_1
  and and_7 (and_7_out, demultiplexer_1_out3, or_5_out);
  assign controlled_buffer_1_out = and_8_out ? C_q : 8'bz;  // Controlled_Buffer controlled_buffer_2
  and and_8 (and_8_out, demultiplexer_1_out2, or_5_out);
  assign controlled_buffer_1_out = and_9_out ? B_q : 8'bz;  // Controlled_Buffer controlled_buffer_3
  and and_9 (and_9_out, demultiplexer_1_out1, or_5_out);
  assign controlled_buffer_1_out = and_10_out ? A_q : 8'bz;  // Controlled_Buffer controlled_buffer_4
  and and_10 (and_10_out, demultiplexer_1_out0, or_5_out);
  assign DI = SR ? controlled_buffer_1_out : 8'bz;  // Controlled_Buffer controlled_buffer_5
  assign DO = not_1_out ? controlled_buffer_1_out : 8'bz;  // Controlled_Buffer controlled_buffer_6
  Demultiplexer #(.select(3)) demultiplexer_1 (
    .out0(demultiplexer_1_out0), .out1(demultiplexer_1_out1), .out2(demultiplexer_1_out2),
    .out3(demultiplexer_1_out3), .out4(demultiplexer_1_out4), .out5(demultiplexer_1_out5),
    .out6(demultiplexer_1_out6), .out7(demultiplexer_1_out7), .in(1'b1), .sel(RS));
  and and_11 (and_11_out, demultiplexer_1_out4, and_1_out);
  and and_12 (and_12_out, demultiplexer_1_out4, or_5_out);
  and and_13 (and_13_out, demultiplexer_1_out5, and_1_out);
  and and_14 (and_14_out, demultiplexer_1_out5, or_5_out);
  and and_15 (and_15_out, demultiplexer_1_out6, and_1_out);
  and and_16 (and_16_out, demultiplexer_1_out6, or_5_out);
  and and_17 (and_17_out, demultiplexer_1_out7, and_1_out);
  and and_18 (and_18_out, demultiplexer_1_out7, or_5_out);
  Register #(.trigger("falling")) E (.D(DI), .en(or_6_out), .clk(CLK), .Q(E_q), .clr(RESET));
  or or_6 (or_6_out, pull_resistor_5_node, and_11_out);
  Register #(.trigger("falling")) F (.D(DI), .en(or_7_out), .clk(CLK), .Q(F_q), .clr(RESET));
  or or_7 (or_7_out, pull_resistor_6_node, and_13_out);
  Register #(.trigger("falling")) H (.D(HI), .en(or_8_out), .clk(CLK), .Q(HO), .clr(RESET));
  assign HI = DI;  // Buffer buffer_1, 8 bits wide
  or or_8 (or_8_out, pull_resistor_7_node, and_6_out, and_15_out);
  Register #(.trigger("falling")) L (.D(LI), .en(or_9_out), .clk(CLK), .Q(LO), .clr(RESET));
  assign LI = DI;  // Buffer buffer_2, 8 bits wide
  or or_9 (or_9_out, pull_resistor_8_node, and_6_out, and_17_out);
  assign controlled_buffer_1_out = and_12_out ? E_q : 8'bz;  // Controlled_Buffer controlled_buffer_7
  assign controlled_buffer_1_out = and_14_out ? F_q : 8'bz;  // Controlled_Buffer controlled_buffer_8
  assign controlled_buffer_1_out = and_16_out ? HO : 8'bz;  // Controlled_Buffer controlled_buffer_9
  assign controlled_buffer_1_out = and_18_out ? LO : 8'bz;  // Controlled_Buffer controlled_buffer_10
  Pull_Resistor pull_resistor_1 (.node(pull_resistor_1_node));
  Pull_Resistor pull_resistor_2 (.node(pull_resistor_2_node));
  Pull_Resistor pull_resistor_3 (.node(pull_resistor_3_node));
  Pull_Resistor pull_resistor_4 (.node(pull_resistor_4_node));
  Pull_Resistor pull_resistor_5 (.node(pull_resistor_5_node));
  Pull_Resistor pull_resistor_6 (.node(pull_resistor_6_node));
  Pull_Resistor pull_resistor_7 (.node(pull_resistor_7_node));
  Pull_Resistor pull_resistor_8 (.node(pull_resistor_8_node));
  Demultiplexer #(.select(3)) demultiplexer_2 (
    .out0(pull_resistor_1_node), .out1(pull_resistor_2_node), .out2(pull_resistor_3_node),
    .out3(pull_resistor_4_node), .out4(pull_resistor_5_node), .out5(pull_resistor_6_node),
    .out6(pull_resistor_7_node), .out7(pull_resistor_8_node), .in(SR), .sel(RSB));
endmodule

module memory_bank (
  input  [7:0] SREG,
  input  [7:0] PI,
  input  [7:0] DI,
  input  ALI,
  input  AHI,
  input  LA,
  input  SA,
  input  CLK,
  input  THL,
  input  RBO,
  input  [7:0] HI,
  input  [7:0] LI,
  input  RESET,
  input  SPD,
  input  SPI,
  input  LSP,
  output [7:0] PO,
  output [4:0] PS,
  output [7:0] DO,
  output PR,
  output PW,
  output [7:0] HO,
  output [7:0] LO
);

  wire and_1_out, and_2_out, and_3_out, and_4_out, and_5_out, and_6_out, and_7_out, and_8_out, and_9_out,
       not_1_out, not_2_out, or_1_out, or_2_out;
  wire [7:0] controlled_buffer_2_out, controlled_buffer_4_out, controlled_buffer_8_out,
       controlled_buffer_11_out, MEM_data, SP_spo, SP_spo_2;

  assign DO = LA ? controlled_buffer_8_out : 8'bz;  // Controlled_Buffer controlled_buffer_1
  assign controlled_buffer_2_out = ALI ? DI : 8'bz;  // Controlled_Buffer controlled_buffer_2
  assign controlled_buffer_2_out = and_1_out ? LI : 8'bz;  // Controlled_Buffer controlled_buffer_3
  or or_1 (or_1_out, ALI, LSP, and_1_out);
  or or_2 (or_2_out, AHI, LSP, and_1_out);
  and and_1 (and_1_out, RBO, THL);
  assign controlled_buffer_4_out = and_1_out ? HI : 8'bz;  // Controlled_Buffer controlled_buffer_4
  Register #(.trigger("falling")) LOW (
    .D(controlled_buffer_2_out), .en(or_1_out), .clk(and_2_out), .Q(LO), .clr(RESET));
  and and_2 (and_2_out, or_1_out, CLK);
  Register #(.trigger("falling")) HIGH (
    .D(controlled_buffer_4_out), .en(or_2_out), .clk(and_3_out), .Q(HO), .clr(RESET));
  assign controlled_buffer_4_out = AHI ? DI : 8'bz;  // Controlled_Buffer controlled_buffer_5
  and and_3 (and_3_out, or_2_out, CLK);
  assign controlled_buffer_4_out = LSP ? SP_spo_2 : 8'bz;  // Controlled_Buffer controlled_buffer_6
  assign controlled_buffer_2_out = LSP ? SP_spo : 8'bz;  // Controlled_Buffer controlled_buffer_7
  assign controlled_buffer_8_out = not_1_out ? MEM_data : 8'bz;  // Controlled_Buffer controlled_buffer_8
  RAM #(.addrWidth(16), .asyncread("true"), .clearpin("true"), .databus("bidir"), .trigger("falling")) MEM (
    .addr({HO, LO}), .we(SA), .oe(LA), .clk(CLK), .data(MEM_data), .clr(RESET));
  not not_1 (not_1_out, and_4_out);
  assign MEM_data = SA ? DI : 8'bz;  // Controlled_Buffer controlled_buffer_9
  stack_ptr SP (.RESET(RESET), .CLK(CLK), .SPD(SPD), .SPI(SPI), .SPO({SP_spo_2, SP_spo}));
  and and_4 (and_4_out, LO[5], LO[6], LO[7], HO[0], HO[1], HO[2], HO[3], HO[4], HO[5], HO[6], HO[7]);
  and and_5 (and_5_out, and_4_out, LA);
  assign controlled_buffer_8_out = and_5_out ? controlled_buffer_11_out : 8'bz;  // Controlled_Buffer controlled_buffer_10
  assign controlled_buffer_11_out = and_6_out ? SREG : 8'bz;  // Controlled_Buffer controlled_buffer_11
  and and_6 (and_6_out, LO[0], LO[1], LO[2], LO[3], LO[4]);
  and and_7 (and_7_out, ~LO[0], LO[1], LO[2], LO[3], LO[4]);  // AND_Gate
  assign controlled_buffer_11_out = and_7_out ? SP_spo_2 : 8'bz;  // Controlled_Buffer controlled_buffer_12
  and and_8 (and_8_out, LO[0], ~LO[1], LO[2], LO[3], LO[4]);  // AND_Gate
  assign controlled_buffer_11_out = and_8_out ? SP_spo : 8'bz;  // Controlled_Buffer controlled_buffer_13
  and and_9 (and_9_out, LO[2], LO[3], LO[4]);
  not not_2 (not_2_out, and_9_out);
  assign controlled_buffer_11_out = PR ? PI : 8'bz;  // Controlled_Buffer controlled_buffer_14
  and and_10 (PR, LA, not_2_out);
  and and_11 (PW, not_2_out, SA);

  assign PO = DI;
  assign PS = LO[4:0];
endmodule

module alu (
  input  AO,
  input  AOH,
  input  AOM,
  input  AOL,
  input  [7:0] BI,
  input  CLK,
  input  RESET,
  input  CI,
  output SZ,
  output RZ,
  output SC,
  output RC,
  output [7:0] BO,
  output SL,
  output RL,
  output SE,
  output RE,
  output SG,
  output RG
);

  wire and_1_out, demultiplexer_1_out0, demultiplexer_1_out1, demultiplexer_1_out2, demultiplexer_1_out3,
       demultiplexer_1_out4, demultiplexer_1_out5, demultiplexer_1_out6, demultiplexer_1_out7,
       demultiplexer_1_out8, demultiplexer_1_out9, demultiplexer_1_out10, demultiplexer_1_out11,
       demultiplexer_1_out12, demultiplexer_1_out13, demultiplexer_1_out14, demultiplexer_1_out15,
       n7485_1_pin2, n7485_1_pin3, n7485_1_pin4, n7485_1_pin5, n7485_1_pin6, n7485_1_pin7, n7485_2_pin5,
       n7485_2_pin6, n7485_2_pin7, n74283_1_pin7, n74283_1_pin9, n74283_2_pin7, not_1_out, not_2_out,
       or_1_out, or_2_out;
  wire [7:0] A_q, B_q, controlled_buffer_3_out, n74283_2_pin4, nand_1_out, or_3_out;

  // NoConnect on demultiplexer_1_out0
  Register A (.D(BI), .en(demultiplexer_1_out3), .clk(CLK), .Q(A_q), .clr(RESET));
  and and_1 (and_1_out, ~A_q[0], ~A_q[1], ~A_q[2], ~A_q[3], ~A_q[4], ~A_q[5], ~A_q[6], ~A_q[7]);  // AND_Gate
  Demultiplexer #(.select(4)) demultiplexer_1 (
    .out0(demultiplexer_1_out0), .out1(demultiplexer_1_out1), .out2(demultiplexer_1_out2),
    .out3(demultiplexer_1_out3), .out4(demultiplexer_1_out4), .out5(demultiplexer_1_out5),
    .out6(demultiplexer_1_out6), .out7(demultiplexer_1_out7), .out8(demultiplexer_1_out8),
    .out9(demultiplexer_1_out9), .out10(demultiplexer_1_out10), .out11(demultiplexer_1_out11),
    .out12(demultiplexer_1_out12), .out13(demultiplexer_1_out13), .out14(demultiplexer_1_out14),
    .out15(demultiplexer_1_out15), .in(1'b1), .sel({AO, AOH, AOM, AOL}));
  // NoConnect on demultiplexer_1_out5
  // NoConnect on demultiplexer_1_out6
  // NoConnect on demultiplexer_1_out7
  Register B (.D(BI), .en(demultiplexer_1_out4), .clk(CLK), .Q(B_q), .clr(RESET));
  assign SZ = demultiplexer_1_out2 ? and_1_out : 1'bz;  // Controlled_Buffer controlled_buffer_1
  not not_1 (not_1_out, and_1_out);
  assign RZ = demultiplexer_1_out2 ? not_1_out : 1'bz;  // Controlled_Buffer controlled_buffer_2
  // NoConnect on demultiplexer_1_out14
  // NoConnect on demultiplexer_1_out15
  _7485 #(.ShowInternalStructure("true")) u_7485_1 (
    .pin1(B_q[3]), .pin2(n7485_1_pin2), .pin3(n7485_1_pin3), .pin4(n7485_1_pin4), .pin5(n7485_1_pin5),
    .pin6(n7485_1_pin6), .pin7(n7485_1_pin7), .pin15(A_q[3]), .pin14(B_q[2]), .pin13(A_q[2]), .pin12(A_q[1]),
    .pin11(B_q[1]), .pin10(A_q[0]), .pin9(B_q[0]));
  or or_1 (or_1_out, demultiplexer_1_out11, demultiplexer_1_out9);
  not not_2 (not_2_out, or_1_out);
  assign controlled_buffer_3_out = not_2_out ? B_q : 8'bz;  // Controlled_Buffer controlled_buffer_3
  assign controlled_buffer_3_out = or_1_out ? ~B_q : 8'bz;  // Controlled_Inverter controlled_inverter_1
  or or_2 (or_2_out, demultiplexer_1_out8, demultiplexer_1_out9, demultiplexer_1_out11, demultiplexer_1_out10);
  _7485 #(.ShowInternalStructure("true")) u_7485_2 (
    .pin1(B_q[7]), .pin2(n7485_1_pin7), .pin3(n7485_1_pin6), .pin4(n7485_1_pin5), .pin5(n7485_2_pin5),
    .pin6(n7485_2_pin6), .pin7(n7485_2_pin7), .pin15(A_q[7]), .pin14(B_q[6]), .pin13(A_q[6]), .pin12(A_q[5]),
    .pin11(B_q[5]), .pin10(A_q[4]), .pin9(B_q[4]));
  _74283 #(.ShowInternalStructure("true")) u_74283_1 (
    .pin1(n74283_2_pin4[5]), .pin2(controlled_buffer_3_out[5]), .pin3(A_q[5]), .pin4(n74283_2_pin4[4]),
    .pin5(A_q[4]), .pin6(controlled_buffer_3_out[4]), .pin7(n74283_1_pin7),
    .pin15(controlled_buffer_3_out[6]), .pin14(A_q[6]), .pin13(n74283_2_pin4[6]), .pin12(A_q[7]),
    .pin11(controlled_buffer_3_out[7]), .pin10(n74283_2_pin4[7]), .pin9(n74283_1_pin9));
  _74283 #(.ShowInternalStructure("true")) u_74283_2 (
    .pin1(n74283_2_pin4[1]), .pin2(controlled_buffer_3_out[1]), .pin3(A_q[1]), .pin4(n74283_2_pin4[0]),
    .pin5(A_q[0]), .pin6(controlled_buffer_3_out[0]), .pin7(n74283_2_pin7),
    .pin15(controlled_buffer_3_out[2]), .pin14(A_q[2]), .pin13(n74283_2_pin4[2]), .pin12(A_q[3]),
    .pin11(controlled_buffer_3_out[3]), .pin10(n74283_2_pin4[3]), .pin9(n74283_1_pin7));
  assign or_3_out = A_q | B_q;  // OR_Gate or_3, 8 bits wide
  assign nand_1_out = ~(A_q & B_q);  // NAND_Gate nand_1, 8 bits wide
  assign BO = demultiplexer_1_out13 ? or_3_out : 8'bz;  // Controlled_Buffer controlled_buffer_4
  assign BO = demultiplexer_1_out12 ? nand_1_out : 8'bz;  // Controlled_Buffer controlled_buffer_5
  Pull_Resistor pull_resistor_1 (.node(n74283_2_pin7));
  assign n74283_2_pin7 = demultiplexer_1_out9 ? 1'b1 : 1'bz;  // Controlled_Buffer controlled_buffer_6
  assign n74283_2_pin7 = demultiplexer_1_out11 ? ~CI : 1'bz;  // Controlled_Inverter controlled_inverter_2
  assign n74283_2_pin7 = demultiplexer_1_out10 ? CI : 1'bz;  // Controlled_Buffer controlled_buffer_7
  assign SL = demultiplexer_1_out1 ? n7485_2_pin7 : 1'bz;  // Controlled_Buffer controlled_buffer_8
  assign RL = demultiplexer_1_out1 ? ~n7485_2_pin7 : 1'bz;  // Controlled_Inverter controlled_inverter_3
  assign SE = demultiplexer_1_out1 ? n7485_2_pin6 : 1'bz;  // Controlled_Buffer controlled_buffer_9
  assign RE = demultiplexer_1_out1 ? ~n7485_2_pin6 : 1'bz;  // Controlled_Inverter controlled_inverter_4
  assign SG = demultiplexer_1_out1 ? n7485_2_pin5 : 1'bz;  // Controlled_Buffer controlled_buffer_10
  assign RG = demultiplexer_1_out1 ? ~n7485_2_pin5 : 1'bz;  // Controlled_Inverter controlled_inverter_5
  assign BO = or_2_out ? n74283_2_pin4 : 8'bz;  // Controlled_Buffer controlled_buffer_11
  assign SC = or_2_out ? n74283_1_pin9 : 1'bz;  // Controlled_Buffer controlled_buffer_12
  assign RC = or_2_out ? ~n74283_1_pin9 : 1'bz;  // Controlled_Inverter controlled_inverter_6
  // also tied to GND on the sheet: {n7485_1_pin2, n7485_1_pin4}
  // also tied to VCC on the sheet: n7485_1_pin3

  // Notes on the sheet:
  //   SC: pull=down
  //   RC: pull=down
  //   SZ: pull=down
  //   RZ: pull=down
  //   SL: pull=down
  //   RL: pull=down
  //   SG: pull=down
  //   RG: pull=down
  //   SE: pull=down
  //   RE: pull=down
endmodule

module control (
  input  [7:0] AL,
  input  [7:0] AH,
  input  [7:0] LI,
  input  [7:0] HI,
  input  Z,
  input  RESET,
  input  CLK,
  output SPI,
  output SPD,
  output SR,
  output [7:0] BO,
  output LSP,
  output AHI,
  output ALI,
  output SA,
  output LA,
  output THL,
  output AOL,
  output AOM,
  output AOH,
  output AO,
  output RBI,
  output RBO,
  output [2:0] RS,
  output [2:0] RSP
);

  wire and_1_out, and_2_out, and_3_out, and_4_out, CNT_pin3, CNT_pin4, CNT_pin5, CNT_pin6, CNT_pin9,
       d_ff_1_q, d_ff_2_q, H, HALT_qn, nor_1_out, not_1_out, not_2_out, not_3_out, or_1_out, or_2_out,
       or_3_out;
  wire [2:0] CNT_pin14;
  wire [6:2] CM_data;
  wire [7:0] P;
  wire [7:3] I;
  wire [7:6] CH_data, CL_data;
  wire [15:0] controlled_buffer_3_out, program_counter_1_do;

  D_Flip_Flop d_ff_1 (.D(CM_data[2]), .clk(CLK), .Q(d_ff_1_q));  // open: Qn, preset, reset
  D_Flip_Flop #(.trigger("falling")) d_ff_2 (.D(d_ff_1_q), .clk(CLK), .Q(d_ff_2_q));  // open: Qn, preset, reset
  ROM CL (.addr({I, CNT_pin14}), .data({CL_data, RBO, RBI, AO, AOH, AOM, AOL}));
  and and_1 (and_1_out, Z, CM_data[4]);
  not not_1 (not_1_out, H);
  // NoConnect on CNT_pin6
  // NoConnect on CNT_pin5
  // NoConnect on CNT_pin4
  // NoConnect on CNT_pin3
  not not_2 (not_2_out, CLK);
  nor nor_1 (nor_1_out, and_2_out, RESET);
  _74161 #(.ShowInternalStructure("true")) CNT (
    .pin1(nor_1_out), .pin2(not_2_out), .pin3(CNT_pin3), .pin4(CNT_pin4), .pin5(CNT_pin5), .pin6(CNT_pin6),
    .pin7(not_1_out), .pin14(CNT_pin14[0]), .pin13(CNT_pin14[1]), .pin12(CNT_pin14[2]), .pin10(not_1_out),
    .pin9(CNT_pin9));  // open: pin15, pin11
  and and_2 (and_2_out, CM_data[2], d_ff_2_q);
  and and_3 (and_3_out, CLK, ~H);  // AND_Gate
  and and_4 (and_4_out, ~Z, CM_data[4]);  // AND_Gate
  S_R_Flip_Flop HALT (.S(CH_data[7]), .R(1'b0), .clk(CLK), .Q(H), .reset(RESET), .Qn(HALT_qn));  // open: preset
  or or_1 (or_1_out, and_1_out, CM_data[3]);
  ROM #(.addrWidth(16)) rom_1 (.addr(controlled_buffer_3_out), .data(P));
  // NoConnect on HALT_qn
  ROM CM (.addr({I, CNT_pin14}), .data({SR, CM_data, SPD, SPI}));
  or or_2 (or_2_out, CL_data[7], SR);
  assign RS = or_2_out ? P[2:0] : 3'bz;  // Controlled_Buffer controlled_buffer_1
  assign RS = CL_data[6] ? RSP : 3'bz;  // Controlled_Buffer controlled_buffer_2
  Register INST (.D(P), .en(CM_data[5]), .clk(CLK), .Q({I, RSP}), .clr(RESET));
  program_counter program_counter_1 (
    .RESET(RESET), .CLK(and_3_out), .DI({HI, LI}), .PCI(or_1_out), .JMP(and_4_out), .DO(program_counter_1_do));
  not not_3 (not_3_out, CH_data[6]);
  assign controlled_buffer_3_out = not_3_out ? program_counter_1_do : 16'bz;  // Controlled_Buffer controlled_buffer_3
  ROM CH (.addr({I, CNT_pin14}), .data({CH_data, LSP, AHI, ALI, SA, LA, THL}));
  assign controlled_buffer_3_out = CH_data[6] ? {AH, AL} : 16'bz;  // Controlled_Buffer controlled_buffer_4
  assign BO = or_3_out ? P : 8'bz;  // Controlled_Buffer controlled_buffer_5
  or or_3 (or_3_out, CH_data[6], CM_data[6]);
  // NoConnect on CL_data[6]
  // NoConnect on CL_data[7]
  // NoConnect on CM_data[2]
  // NoConnect on CM_data[3]
  // NoConnect on CM_data[4]
  // NoConnect on CM_data[5]
  // also tied to VCC on the sheet: CNT_pin9

  // Other names for the same wires on the sheet: C = CLK; I[2:0] = RSP; R = RESET

  // Notes on the sheet:
  //   contents of CL (hex, n*v repeats v):
  //   0 63 a4 58 5*0 63 4 58 5*0 63 a4 59 5*0 63 4 59 5*0 63 a4 5a 5*0 63 4 5a 5*0 63 a4 5b 5*0 63 4 5b
  //   5*0 63 a4 5c 5*0 63 4 5c 5*0 63 a4 5c 5*0 63 4 5c 5*0 63 a4 9 5*0 63 4 1 13*0 50 7*0 20 50 8*0 50
  //   5*0 20 60 8*0 60 15*0 10 5*0 20 60 8*0 50 6*0 60 16*0 50 13*0 63 2 6*0 3 2
  //   contents of rom_1 (hex, n*v repeats v):
  //   c8 9 c8 0 a8 0 17 e8 1 c8 12 c8 0 a8 0 25 e8 1 a8 0 9 e8 1 7a 2 9a ff f8 7a ff 9a ff f9 d6 d7 e8 1
  //   88 ff fa 48 1 40 0 a8 0 37 e0 79 ff a8 0 39 e8 1 79 fd 99 ff f9 d6 d7 e8 1
  //   contents of CM (hex, n*v repeats v):
  //   20 8 0 c 4*0 20 8 40 c 4*0 20 8 0 c 4*0 20 8 40 c 4*0 20 8 0 c 4*0 20 8 40 c 4*0 20 8 0 c 4*0 20 8
  //   40 c 4*0 20 8 0 c 4*0 20 8 40 c 4*0 20 8 0 c 4*0 20 8 40 c 4*0 20 8 0 c 4*0 20 8 40 c 4*0 20 88 c
  //   5*0 20 48 c 5*0 20 0 c 5*0 20 48 48 c 4*0 20 0 c 5*0 20 48 48 c 12*0 20 48 48 c 4*0 20 0 c 5*0 20 48
  //   48 c 4*0 20 0 0 e 4*0 20 8 40 e 4*0 20 1 0 c 12*0 20 0 14 5*0 20 48 14 5*0 20 7*0 20
  //   contents of CH (hex, n*v repeats v):
  //   129*0 1 2 6*0 10 8 2 5*0 1 4 6*0 10 8 4 13*0 10 8 1 5*0 1 4 6*0 10 8 40 5*0 20 4 6*0 20 4 7*0 20 2
  //   29*0 80 7*0 80
endmodule

module stack_ptr (
  input  RESET,
  input  CLK,
  input  SPD,
  input  SPI,
  output [15:0] SPO
);

  wire and_1_out, and_2_out, not_1_out, not_2_out, SP0_pin11, SP0_pin12, SP0_pin13, SP2_pin4, SP2_pin5,
       SP2_pin12, SP2_pin13;
  wire [15:0] SP0_pin15;

  not not_1 (not_1_out, and_1_out);
  and and_1 (and_1_out, ~CLK, SPD);  // AND_Gate
  not not_2 (not_2_out, and_2_out);
  and and_2 (and_2_out, ~CLK, SPI);  // AND_Gate
  _74193 #(.ShowInternalStructure("true")) SP0 (
    .pin1(SP0_pin15[1]), .pin2(SPO[1]), .pin3(SPO[0]), .pin4(not_1_out), .pin5(not_2_out), .pin6(SPO[2]),
    .pin7(SPO[3]), .pin15(SP0_pin15[0]), .pin13(SP0_pin13), .pin12(SP0_pin12), .pin11(SP0_pin11),
    .pin10(SP0_pin15[2]), .pin9(SP0_pin15[3]));  // open: pin14
  not not_3 (SP0_pin11, RESET);
  _74193 #(.ShowInternalStructure("true")) SP2 (
    .pin1(SP0_pin15[9]), .pin2(SPO[9]), .pin3(SPO[8]), .pin4(SP2_pin4), .pin5(SP2_pin5), .pin6(SPO[10]),
    .pin7(SPO[11]), .pin15(SP0_pin15[8]), .pin13(SP2_pin13), .pin12(SP2_pin12), .pin11(SP0_pin11),
    .pin10(SP0_pin15[10]), .pin9(SP0_pin15[11]));  // open: pin14
  _74193 #(.ShowInternalStructure("true")) SP1 (
    .pin1(SP0_pin15[5]), .pin2(SPO[5]), .pin3(SPO[4]), .pin4(SP0_pin13), .pin5(SP0_pin12), .pin6(SPO[6]),
    .pin7(SPO[7]), .pin15(SP0_pin15[4]), .pin13(SP2_pin4), .pin12(SP2_pin5), .pin11(SP0_pin11),
    .pin10(SP0_pin15[6]), .pin9(SP0_pin15[7]));  // open: pin14
  _74193 #(.ShowInternalStructure("true")) SP3 (
    .pin1(SP0_pin15[13]), .pin2(SPO[13]), .pin3(SPO[12]), .pin4(SP2_pin13), .pin5(SP2_pin12), .pin6(SPO[14]),
    .pin7(SPO[15]), .pin15(SP0_pin15[12]), .pin11(SP0_pin11), .pin10(SP0_pin15[14]), .pin9(SP0_pin15[15]));  // open: pin14, pin13, pin12
  // also tied to GND on the sheet: SP0_pin15[5]
  // also tied to VCC on the sheet: {SP0_pin15[0], SP0_pin15[1], SP0_pin15[2], SP0_pin15[3], SP0_pin15[4], SP0_pin15[6], SP0_pin15[7], SP0_pin15[8], SP0_pin15[9], SP0_pin15[10], SP0_pin15[11], SP0_pin15[12], SP0_pin15[13], SP0_pin15[14], SP0_pin15[15]}

  // Notes on the sheet:
  //   RESET: pull=down
endmodule

module program_counter (
  input  RESET,
  input  CLK,
  input  [15:0] DI,
  input  PCI,
  input  JMP,
  output [15:0] DO
);

  wire and_2_out, n74161_1_pin1, n74161_1_pin9, n74161_1_pin15, n74161_2_pin2, n74161_2_pin15, n74161_3_pin2,
       n74161_3_pin15, n74161_4_pin2, not_3_out, not_4_out, not_5_out, not_6_out;

  _74161 #(.ShowInternalStructure("true")) u_74161_1 (
    .pin1(n74161_1_pin1), .pin2(CLK), .pin3(DI[0]), .pin4(DI[1]), .pin5(DI[2]), .pin6(DI[3]), .pin7(PCI),
    .pin15(n74161_1_pin15), .pin14(DO[0]), .pin13(DO[1]), .pin12(DO[2]), .pin11(DO[3]), .pin10(PCI),
    .pin9(n74161_1_pin9));
  not not_1 (n74161_1_pin1, RESET);
  not not_2 (n74161_1_pin9, JMP);
  not not_3 (not_3_out, n74161_1_pin15);
  _74161 #(.ShowInternalStructure("true")) u_74161_2 (
    .pin1(n74161_1_pin1), .pin2(n74161_2_pin2), .pin3(DI[4]), .pin4(DI[5]), .pin5(DI[6]), .pin6(DI[7]),
    .pin7(PCI), .pin15(n74161_2_pin15), .pin14(DO[4]), .pin13(DO[5]), .pin12(DO[6]), .pin11(DO[7]),
    .pin10(PCI), .pin9(n74161_1_pin9));
  and and_1 (n74161_2_pin2, not_4_out, not_3_out);
  and and_2 (and_2_out, CLK, JMP);
  not not_4 (not_4_out, and_2_out);
  not not_5 (not_5_out, n74161_2_pin15);
  _74161 #(.ShowInternalStructure("true")) u_74161_3 (
    .pin1(n74161_1_pin1), .pin2(n74161_3_pin2), .pin3(DI[8]), .pin4(DI[9]), .pin5(DI[10]), .pin6(DI[11]),
    .pin7(PCI), .pin15(n74161_3_pin15), .pin14(DO[8]), .pin13(DO[9]), .pin12(DO[10]), .pin11(DO[11]),
    .pin10(PCI), .pin9(n74161_1_pin9));
  and and_3 (n74161_3_pin2, not_4_out, not_5_out);
  not not_6 (not_6_out, n74161_3_pin15);
  _74161 #(.ShowInternalStructure("true")) u_74161_4 (
    .pin1(n74161_1_pin1), .pin2(n74161_4_pin2), .pin3(DI[12]), .pin4(DI[13]), .pin5(DI[14]), .pin6(DI[15]),
    .pin7(PCI), .pin14(DO[12]), .pin13(DO[13]), .pin12(DO[14]), .pin11(DO[15]), .pin10(PCI),
    .pin9(n74161_1_pin9));  // open: pin15
  and and_4 (n74161_4_pin2, not_4_out, not_6_out);
endmodule

module sreg (
  input  SZ,
  input  RZ,
  input  SG,
  input  RG,
  input  SE,
  input  RE,
  input  SL,
  input  RL,
  input  SC,
  input  RC,
  input  SH,
  input  RH,
  input  RESET,
  output Z,
  output G,
  output E,
  output L,
  output C,
  output H
);

  wire or_1_out, or_2_out, or_3_out, or_4_out, or_5_out, or_6_out, undriven, undriven_2, undriven_3,
       undriven_4, undriven_5, undriven_6, undriven_7, undriven_8, undriven_9, undriven_10, undriven_11,
       undriven_12, undriven_13, undriven_14, undriven_15, undriven_16, undriven_17, undriven_18;

  S_R_Flip_Flop #(.trigger("high")) s_r_ff_1 (
    .S(undriven), .R(undriven_2), .clk(undriven_3), .Q(Z), .reset(or_1_out), .preset(SZ));  // open: Qn
  // NoConnect on undriven
  // NoConnect on undriven_2
  // NoConnect on undriven_3
  or or_1 (or_1_out, RZ, RESET);
  S_R_Flip_Flop #(.trigger("high")) s_r_ff_2 (
    .S(undriven_4), .R(undriven_5), .clk(undriven_6), .Q(G), .reset(or_2_out), .preset(SG));  // open: Qn
  // NoConnect on undriven_4
  // NoConnect on undriven_5
  // NoConnect on undriven_6
  or or_2 (or_2_out, RG, RESET);
  S_R_Flip_Flop #(.trigger("high")) s_r_ff_3 (
    .S(undriven_7), .R(undriven_8), .clk(undriven_9), .Q(E), .reset(or_3_out), .preset(SE));  // open: Qn
  // NoConnect on undriven_7
  // NoConnect on undriven_8
  // NoConnect on undriven_9
  or or_3 (or_3_out, RE, RESET);
  S_R_Flip_Flop #(.trigger("high")) s_r_ff_4 (
    .S(undriven_10), .R(undriven_11), .clk(undriven_12), .Q(L), .reset(or_4_out), .preset(SL));  // open: Qn
  // NoConnect on undriven_10
  // NoConnect on undriven_11
  // NoConnect on undriven_12
  or or_4 (or_4_out, RL, RESET);
  S_R_Flip_Flop #(.trigger("high")) s_r_ff_5 (
    .S(undriven_13), .R(undriven_14), .clk(undriven_15), .Q(C), .reset(or_5_out), .preset(SC));  // open: Qn
  // NoConnect on undriven_13
  // NoConnect on undriven_14
  // NoConnect on undriven_15
  or or_5 (or_5_out, RC, RESET);
  S_R_Flip_Flop #(.trigger("high")) s_r_ff_6 (
    .S(undriven_16), .R(undriven_17), .clk(undriven_18), .Q(H), .reset(or_6_out), .preset(SH));  // open: Qn
  // NoConnect on undriven_16
  // NoConnect on undriven_17
  // NoConnect on undriven_18
  or or_6 (or_6_out, RH, RESET);

  // Notes on the sheet:
  //   RL: pull=down
  //   SC: pull=down
  //   RC: pull=down
endmodule

module ports (
  input  [4:0] PS,
  input  WRITE,
  input  READ,
  input  [7:0] PAI,
  input  CLK,
  input  [7:0] DI,
  input  RESET,
  output [7:0] PAO,
  output [7:0] PO
);

  wire and_1_out, not_1_out;
  wire [1:0] controlled_buffer_1_out;

  and and_1 (and_1_out, ~PS[2], PS[3], PS[4]);  // AND_Gate
  not not_1 (not_1_out, and_1_out);
  assign controlled_buffer_1_out = not_1_out ? 2'b11 : 2'bz;  // Controlled_Buffer controlled_buffer_1
  assign controlled_buffer_1_out = and_1_out ? PS[1:0] : 2'bz;  // Controlled_Buffer controlled_buffer_2
  dio PORTA (
    .SEL(controlled_buffer_1_out), .W(WRITE), .R(READ), .CLK(CLK), .DI(DI), .RESET(RESET), .PININ(PAI),
    .DO(PO), .PINOUT(PAO));
endmodule

module dio (
  input  [1:0] SEL,
  input  W,
  input  R,
  input  CLK,
  input  [7:0] DI,
  input  RESET,
  input  [7:0] PININ,
  output [7:0] DO,
  output [7:0] PINOUT
);

  wire and_1_out, and_2_out, and_3_out, and_4_out, and_5_out, demultiplexer_1_out0, demultiplexer_1_out1,
       demultiplexer_1_out2, demultiplexer_1_out3, nand_1_out, nand_2_out, nand_3_out, nand_4_out,
       nand_5_out, nand_6_out, nand_7_out, nand_8_out, pull_resistor_1_node, pull_resistor_2_node,
       pull_resistor_3_node, pull_resistor_4_node, pull_resistor_5_node, pull_resistor_6_node,
       pull_resistor_7_node, pull_resistor_8_node;
  wire [7:0] DDR_q, PUSH_q;

  Demultiplexer #(.select(2)) demultiplexer_1 (
    .out0(demultiplexer_1_out0), .out1(demultiplexer_1_out1), .out2(demultiplexer_1_out2),
    .out3(demultiplexer_1_out3), .in(1'b1), .sel(SEL));
  // NoConnect on demultiplexer_1_out3
  and and_1 (and_1_out, demultiplexer_1_out0, W);
  and and_2 (and_2_out, demultiplexer_1_out1, W);
  Register #(.trigger("falling")) DDR (.D(DI), .en(and_1_out), .clk(CLK), .Q(DDR_q), .clr(RESET));
  Register #(.trigger("falling")) PUSH (.D(DI), .en(and_2_out), .clk(CLK), .Q(PUSH_q), .clr(RESET));
  and and_3 (and_3_out, R, demultiplexer_1_out0);
  assign DO = and_3_out ? DDR_q : 8'bz;  // Controlled_Buffer controlled_buffer_1
  and and_4 (and_4_out, R, demultiplexer_1_out1);
  assign DO = and_4_out ? PUSH_q : 8'bz;  // Controlled_Buffer controlled_buffer_2
  and and_5 (and_5_out, R, demultiplexer_1_out2);
  assign DO = and_5_out ? PININ : 8'bz;  // Controlled_Buffer controlled_buffer_3
  nand nand_1 (nand_1_out, PUSH_q[7], ~DDR_q[7]);  // NAND_Gate
  Pull_Resistor #(.pull(1)) pull_resistor_1 (.node(pull_resistor_1_node));
  assign PININ[5] = DDR_q[5] ? PUSH_q[5] : 1'bz;  // Controlled_Buffer controlled_buffer_4
  assign PININ[6] = DDR_q[6] ? PUSH_q[6] : 1'bz;  // Controlled_Buffer controlled_buffer_5
  assign PININ[7] = DDR_q[7] ? PUSH_q[7] : 1'bz;  // Controlled_Buffer controlled_buffer_6
  nand nand_2 (nand_2_out, PUSH_q[6], ~DDR_q[6]);  // NAND_Gate
  nand nand_3 (nand_3_out, PUSH_q[5], ~DDR_q[5]);  // NAND_Gate
  nand nand_4 (nand_4_out, PUSH_q[4], ~DDR_q[4]);  // NAND_Gate
  Pull_Resistor #(.pull(1)) pull_resistor_2 (.node(pull_resistor_2_node));
  Pull_Resistor #(.pull(1)) pull_resistor_3 (.node(pull_resistor_3_node));
  Transistor transistor_1 (.in(pull_resistor_3_node), .out(PININ[5]), .gate(nand_3_out));
  Pull_Resistor #(.pull(1)) pull_resistor_4 (.node(pull_resistor_4_node));
  Transistor transistor_2 (.in(pull_resistor_4_node), .out(PININ[6]), .gate(nand_2_out));
  Transistor transistor_3 (.in(pull_resistor_1_node), .out(PININ[7]), .gate(nand_1_out));
  assign PININ[2] = DDR_q[2] ? PUSH_q[2] : 1'bz;  // Controlled_Buffer controlled_buffer_7
  assign PININ[3] = DDR_q[3] ? PUSH_q[3] : 1'bz;  // Controlled_Buffer controlled_buffer_8
  assign PININ[4] = DDR_q[4] ? PUSH_q[4] : 1'bz;  // Controlled_Buffer controlled_buffer_9
  nand nand_5 (nand_5_out, PUSH_q[3], ~DDR_q[3]);  // NAND_Gate
  nand nand_6 (nand_6_out, PUSH_q[2], ~DDR_q[2]);  // NAND_Gate
  Pull_Resistor #(.pull(1)) pull_resistor_5 (.node(pull_resistor_5_node));
  Pull_Resistor #(.pull(1)) pull_resistor_6 (.node(pull_resistor_6_node));
  Pull_Resistor #(.pull(1)) pull_resistor_7 (.node(pull_resistor_7_node));
  Transistor transistor_4 (.in(pull_resistor_7_node), .out(PININ[3]), .gate(nand_5_out));
  Transistor transistor_5 (.in(pull_resistor_2_node), .out(PININ[4]), .gate(nand_4_out));
  assign PININ[0] = DDR_q[0] ? PUSH_q[0] : 1'bz;  // Controlled_Buffer controlled_buffer_10
  assign PININ[1] = DDR_q[1] ? PUSH_q[1] : 1'bz;  // Controlled_Buffer controlled_buffer_11
  nand nand_7 (nand_7_out, PUSH_q[1], ~DDR_q[1]);  // NAND_Gate
  nand nand_8 (nand_8_out, PUSH_q[0], ~DDR_q[0]);  // NAND_Gate
  Pull_Resistor #(.pull(1)) pull_resistor_8 (.node(pull_resistor_8_node));
  Transistor transistor_6 (.in(pull_resistor_8_node), .out(PININ[0]), .gate(nand_8_out));
  Transistor transistor_7 (.in(pull_resistor_5_node), .out(PININ[1]), .gate(nand_7_out));
  Transistor transistor_8 (.in(pull_resistor_6_node), .out(PININ[2]), .gate(nand_6_out));

  assign PINOUT = PININ;

  // Notes on the sheet:
  //   PULL
endmodule
